# Fritzing sketch Schematic (saved by Fritzing 1.0.1rc)
breadboards: 1

parts:
  Bauteil1 = Arduino Uno (Rev3)
  433_MHz_Transmitter = RF-LINK_TX [package=rf-link_tx]
  DHT22 = Humidity and Temperature Sensor RHT03
  Heating_Indicator_LED = LED - 3mm [color="Red (633nm)" current=0.030 package="3 mm [THT]"]
  Tri-State_Switch_Left_Off_Right = SPST Switch [package=switch-spst-smd-a]
  R1 = Resistor [tolerance=±5% resistance=220 package="0603 [SMD]"]

nets:
  N1: Bauteil1.D8, Tri-State_Switch_Left_Off_Right.P
  N2: Bauteil1.D9_PWM, Tri-State_Switch_Left_Off_Right.O
  N3: Bauteil1.D2, R1.Pin_1
  N4: Bauteil1.D3_PWM, DHT22.Data-signal
  N5: Bauteil1.D4, 433_MHz_Transmitter.DATA
  5V: Bauteil1.5V, 433_MHz_Transmitter.+5V, DHT22.Vcc
  GND: Bauteil1.GND, 433_MHz_Transmitter.GND, DHT22.GND_1, Heating_Indicator_LED.anode, Tri-State_Switch_Left_Off_Right.S
  N6: Heating_Indicator_LED.cathode, R1.Pin_0
